# Fritzing sketch SSPMeteo-ESQUEMA (copia) (saved by Fritzing 0.9.2b)
circuit board: 3.50866cm x 5.31575cm

parts:
  R1 = Resistor [tolerance=±5% resistance=10k package=THT]
  R2 = Resistor [tolerance=±5% resistance=10k package=THT]
  Emisor_RF433 = RF-LINK_TX [package=rf-link_tx]
  ANT1 = Antenna
  SSPMeteo = Arduino Uno (Rev3)
  Veleta = Basic Force Sensing Resistor (FSR) [package=THT]
  DHT22 = Humidity and Temperature Sensor RHT03
  Anemom = HALL-EFFECT [package=sc70]
  Lluvia = HALL-EFFECT [package=sc70]

nets:
  VCC: R1.Pin_0, SSPMeteo.5V, Veleta.pin_0, DHT22.Vcc, Anemom.VCC, Lluvia.VCC
  N1: R1.Pin_1, SSPMeteo.D4, DHT22.Data-signal
  GND: R2.Pin_0, Emisor_RF433.GND, SSPMeteo.GND, DHT22.GND_2, Anemom.GND, Lluvia.GND
  N2: R2.Pin_1, SSPMeteo.A0, Veleta.pin_1
  N3: Emisor_RF433.ANT, ANT1.antenna_lead
  N4: Emisor_RF433.DATA, SSPMeteo.D7
  +5V: Emisor_RF433.+5V, SSPMeteo.VIN
  N5: SSPMeteo.D3_PWM, Anemom.OUT

notes:
  SSPMeteo
  T/H
  R
  5V
  GND
  WD
  WS
  DATA
  VCC
  RF433
  sensores
  SSPMeteo, Estacion meteorologica, 1.0
  Anemometro y lluvia usan resistencias pullup internas.
  NO VALIDO
