# Fritzing sketch SSPMeteo2-ESQUEMA (BME280) (saved by Fritzing 0.9.3b)
circuit board: 3.50866cm x 5.31575cm

parts:
  R = Resistor [tolerance=±5% resistance=10k package=THT]
  Anemometro = Reed switch [package=THT]
  WeMos_D1_R2 = WeMos D1 Mini
  Temp_Humed_y_Pres = BME280 Breakout
  J3 = Camdenboss CTB0158-4 [part_number=CTB0158-4 package=THT]
  J4 = Camdenboss CTB0158-6 [part_number=CTB0158-6 package=THT]
  Veleta = Basic Force Sensing Resistor (FSR) [package=THT]
  Pluviometro = Reed switch [package=THT]

nets:
  3V3: R.Pin_0, WeMos_D1_R2.3V3, Temp_Humed_y_Pres.3.3V, J4.terminal_5
  N1: R.Pin_1, WeMos_D1_R2.A0, J4.terminal_3, Veleta.pin_1
  N2: Anemometro.pin_1, WeMos_D1_R2.G, Temp_Humed_y_Pres.GND, J3.pin1, J3.pin2, J3.pin3, J3.pin4, J3.terminal_1, J3.terminal_2, J3.terminal_3, J3.terminal_4, Veleta.pin_0, Pluviometro.pin_1
  N3: Anemometro.pin_2, WeMos_D1_R2.D7, J4.terminal_1
  N4: WeMos_D1_R2.D1, Temp_Humed_y_Pres.SCK/SCL, J4.terminal_4
  N5: WeMos_D1_R2.D2, Temp_Humed_y_Pres.SDI/SDA, J4.terminal_6
  N6: WeMos_D1_R2.D6, J4.terminal_2, Pluviometro.pin_2

notes:
  SSPMeteo
  T/H
  R
  5V
  GND
  WD
  WS
  DATA
  VCC
  RF433
  sensores
  SSPMeteo2, Estacion meteorologica, 1.0
  Anemometro y pluviometro usan resistencias pullup internas.
  NO VALIDO
  cable blanco
  1
  2
  3
  4
  5
  6
  9
  8
  10
  7
  SDA
  SCL
