# Fritzing sketch SSPMeteo2-ESQUEMA (saved by Fritzing 0.9.3b)

parts:
  R = Resistor [tolerance=±5% resistance=10k package=THT]
  Pluviometro = Reed switch [package=THT]
  WeMos_D1_R2 = WeMos D1 Mini
  Temp_Humed_y_Pres = BME280 Breakout
  J4 = Camdenboss CTB0158-6 [part_number=CTB0158-6 package=THT]
  Veleta = Basic Force Sensing Resistor (FSR) [package=THT]
  Anemometro = Reed switch [package=THT]
  part = Resistor [tolerance=±5% resistance=10k package=THT]
  3V3 = Header 1 [package=1x01_offset]
  SDA = Header 1 [package=1x01_offset]
  SCL = Header 1 [package=1x01_offset]
  GND = Header 1 [package=1x01_offset]
  D6 = Header 1 [package=1x01_offset]
  D7 = Header 1 [package=1x01_offset]
  A0 = Header 1 [package=1x01_offset]
  J6 = Camdenboss CTB0158-10 [part_number=CTB0158-10 package=THT]
  J7 = Camdenboss CTB0158-3 [part_number=CTB0158-3 package=THT]
  D4 = Header 1 [package=1x01_offset]
  DHT22 = Humidity and Temperature Sensor DHT22
  J3 = Camdenboss CTB0158-4 [part_number=CTB0158-4 package=THT]

nets:
  3V3: R.Pin_0, WeMos_D1_R2.3V3, Temp_Humed_y_Pres.3.3V, J4.terminal_5, DHT22.Vcc
  N1: R.Pin_1, WeMos_D1_R2.A0, J4.terminal_3, Veleta.pin_1
  N2: Pluviometro.pin_1, WeMos_D1_R2.G, Temp_Humed_y_Pres.GND, Veleta.pin_0, Anemometro.pin_1, DHT22.GND_2, J3.pin1, J3.pin2, J3.pin3, J3.pin4, J3.terminal_1, J3.terminal_2, J3.terminal_3, J3.terminal_4
  N3: Pluviometro.pin_2, WeMos_D1_R2.D7, J4.terminal_1
  N4: WeMos_D1_R2.D1, Temp_Humed_y_Pres.SCK/SCL, J4.terminal_4
  N5: WeMos_D1_R2.D2, Temp_Humed_y_Pres.SDI/SDA, J4.terminal_6
  N6: WeMos_D1_R2.D4, DHT22.Data-signal
  N7: WeMos_D1_R2.D6, J4.terminal_2, Anemometro.pin_2
  BME280 rojo - 3V3: part.Pin_0, 3V3.1, J6.terminal_5
  Veleta vede: part.Pin_1, A0.1, J6.terminal_3
  BME280 marron - SDA: SDA.1, J6.terminal_6
  BME280 verde - SCL: SCL.1, J6.terminal_4
  Anemometro marron/BME280 blanco - GND/DHT22 azul - VCC/Pluviometro rojo/Veleta rojo: GND.1, J6.pin7, J6.pin8, J6.pin9, J6.pin10, J6.terminal_7, J6.terminal_8, J6.terminal_9, J6.terminal_10, J7.terminal_1
  Anemometro blanco: D6.1, J6.terminal_2
  Pluviometro verde: D7.1, J6.terminal_1
  DHT22 naranja- VCC: J6.pin5, J7.terminal_3
  DHT22 blanco/naranja -SIGNAL: J7.terminal_2, D4.1

notes:
  SSPMeteo
  T/H
  R
  5V
  GND
  WD
  WS
  DATA
  VCC
  RF433
  sensores
  SSPMeteo2, Estacion meteorologica, 1.0
  Conexiones
  NO VALIDO
  verde
  1
  2
  3
  4
  5
  6
  9
  8
  10
  7
  SDA
  SCL
  rojo
  blanco
  marron
  amarillo
  negro
  INVALIDO
  11
  12
  13

custom parts:
  Humidity and Temperature Sensor DHT22: Digital relative humidity & temperature sensor DHT22
